// Logisim project NARCY.circ as structural Verilog: 2 circuits, main circuit main
module main (
);

  wire clk_PC, clk_POR, clk_RAM_DATA, flg_RAM_WRITE, por_1_out, registerreadwriteprotection_1_clkout;
  wire [7:0] GPR_A_q, RAM_DATA, registerreadwriteprotection_1_registerin;
  wire [15:0] undriven;

  POR por_1 (.out(por_1_out));
  Register #(.width(16)) AR ();  // open: D, en, Q, clk, clr
  // Probe on undriven
  RAM #(.addrWidth(16), .enables("line")) ram_1 (
    .addr(undriven), .we(flg_RAM_WRITE), .clk(clk_RAM_DATA), .din(RAM_DATA), .dout(RAM_DATA));
  // Switch switch_1: pin names not known; wires that end beside it: clk_POR, por_1_out, clk_POR
  // Probe on RAM_DATA
  Register PC (.clk(clk_PC), .clr(clk_POR));  // open: D, en, Q
  Register GPR_A (
    .D(registerreadwriteprotection_1_registerin), .Q(GPR_A_q), .clk(registerreadwriteprotection_1_clkout));  // open: en, clr
  RegisterReadWriteProtection registerreadwriteprotection_1 (
    .RegisterIn(registerreadwriteprotection_1_registerin), .ClkOut(registerreadwriteprotection_1_clkout),
    .Dout(GPR_A_q));  // open: write, Din, Clk, RegisterOut
  Register GPR_B ();  // open: D, en, Q, clk, clr
  Register GPR_C ();  // open: D, en, Q, clk, clr
  Register IR ();  // open: D, en, Q, clk, clr
endmodule

module RegisterReadWriteProtection (
  input  [7:0] RegisterOut,
  input  write,
  input  [7:0] Din,
  input  Clk,
  output [7:0] Dout,
  output [7:0] RegisterIn,
  output ClkOut
);

  wire not_1_out;

  assign Dout = not_1_out ? RegisterOut : 8'bz;  // Controlled_Buffer controlled_buffer_1
  not not_1 (not_1_out, write);
  assign RegisterIn = write ? Din : 8'bz;  // Controlled_Buffer controlled_buffer_2

  assign ClkOut = Clk;

  // Notes on the sheet:
  //   write: pull=down
endmodule
